# Fritzing sketch schematic (saved by Fritzing 0.9.6b)
breadboards: 1

parts:
  Arduino_Nano_33_BLE = Arduino Nano 33 BLE Sense
  Pause_Exec = Pushbutton [package="[THT]"]
  Terminate_Exec = Pushbutton [package="[THT]"]
  Calibrate_IMU = Pushbutton [package="[THT]"]
  U1 = LCD-16X2 [package=lcd-16x2_noholes]

nets:
  GND: Arduino_Nano_33_BLE.GND, Arduino_Nano_33_BLE.A7, Pause_Exec.Pin_3, Pause_Exec.Pin_4, Terminate_Exec.Pin_3, Terminate_Exec.Pin_4, Calibrate_IMU.Pin_3, Calibrate_IMU.Pin_4, U1.VSS, U1.VO, U1.R_W, U1.K
  N1: Arduino_Nano_33_BLE.D2, Calibrate_IMU.Pin_1, Calibrate_IMU.Pin_2
  N2: Arduino_Nano_33_BLE.D3~, Terminate_Exec.Pin_1, Terminate_Exec.Pin_2
  N3: Arduino_Nano_33_BLE.D4, Pause_Exec.Pin_1, Pause_Exec.Pin_2
  N4: Arduino_Nano_33_BLE.D5~, U1.DB7
  N5: Arduino_Nano_33_BLE.D6~, U1.DB6
  N6: Arduino_Nano_33_BLE.D7, U1.DB5
  N7: Arduino_Nano_33_BLE.D8, U1.DB4
  N8: Arduino_Nano_33_BLE.D9~, U1.E
  N9: Arduino_Nano_33_BLE.D10~, U1.RS
  +5V: Arduino_Nano_33_BLE.D11/MOSI, Arduino_Nano_33_BLE.+5V, U1.VDD
  N10: Arduino_Nano_33_BLE.3V3, U1.A

custom parts:
  Arduino Nano 33 BLE Sense: The Nano 33 BLE Sense (without headers) is Arduino’s 3.3V AI enabled board in the smallest available form factor: 45x18mm! The Arduino Nano 33 BLE Sense is a completely new board on a well-known form factor. It comes with a series of embedded sensors: 9 axis inertial sensor: what makes this board ideal for wearable devices humidity, and temperature sensor: to get highly accurate measurements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
