# Fritzing sketch wiring (saved by Fritzing 0.9.6b)
breadboards: 1

parts:
  Arduino_Nano_33_BLE = Arduino Nano 33 BLE Sense
  Pause_Exec = Pushbutton [package="[THT]"]
  Terminate_Exec = Pushbutton [package="[THT]"]
  Calibrate_IMU = Pushbutton [package="[THT]"]
  Part1 = LCD1602-I2C
  JP1 = Jumper [package=sj_2s]

nets:
  GND: Arduino_Nano_33_BLE.GND, Arduino_Nano_33_BLE.A7, Pause_Exec.Pin_3, Pause_Exec.Pin_4, Terminate_Exec.Pin_3, Terminate_Exec.Pin_4, Calibrate_IMU.Pin_3, Calibrate_IMU.Pin_4, Part1.GND, JP1.2
  N1: Arduino_Nano_33_BLE.D2, Terminate_Exec.Pin_1, Terminate_Exec.Pin_2
  N2: Arduino_Nano_33_BLE.D3~, Pause_Exec.Pin_1, Pause_Exec.Pin_2
  N3: Arduino_Nano_33_BLE.D4, Calibrate_IMU.Pin_1, Calibrate_IMU.Pin_2
  N4: Arduino_Nano_33_BLE.D5~, JP1.1
  +5V: Arduino_Nano_33_BLE.D11/MOSI, Arduino_Nano_33_BLE.+5V, Part1.VCC
  N5: Arduino_Nano_33_BLE.A5, Part1.SCL
  N6: Arduino_Nano_33_BLE.A4, Part1.SDA

custom parts:
  Arduino Nano 33 BLE Sense: The Nano 33 BLE Sense (without headers) is Arduino’s 3.3V AI enabled board in the smallest available form factor: 45x18mm! The Arduino Nano 33 BLE Sense is a completely new board on a well-known form factor. It comes with a series of embedded sensors: 9 axis inertial sensor: what makes this board ideal for wearable devices humidity, and temperature sensor: to get highly accurate measurements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
  LCD1602-I2C: A standard character display, usually with 2x16 characters. Comes in many colors with LCM1602 IIC attached.
